// Logisim project CRC.circ as structural Verilog: 3 circuits, main circuit CRC
module CRC (
  input  [7:0] A,
  input  [3:0] B,
  output [10:0] C
);

  wire [2:0] sub_4_first_1_left, sub_4_later_1_left, sub_4_later_2_left, sub_4_later_3_left,
       sub_4_later_4_left, sub_4_later_5_left, sub_4_later_6_left;

  sub_4_first sub_4_first_1 (.subee(A[7:4]), .suber(B), .left(sub_4_first_1_left));  // open: subed
  sub_4_later sub_4_later_1 (
    .\new (A[3]), .subee(sub_4_first_1_left), .suber(B), .left(sub_4_later_1_left));  // open: subed
  sub_4_later sub_4_later_2 (
    .\new (A[2]), .subee(sub_4_later_1_left), .suber(B), .left(sub_4_later_2_left));  // open: subed
  sub_4_later sub_4_later_3 (
    .\new (A[1]), .subee(sub_4_later_2_left), .suber(B), .left(sub_4_later_3_left));  // open: subed
  sub_4_later sub_4_later_4 (
    .\new (A[0]), .subee(sub_4_later_3_left), .suber(B), .left(sub_4_later_4_left));  // open: subed
  sub_4_later sub_4_later_5 (
    .\new (1'b0), .subee(sub_4_later_4_left), .suber(B), .left(sub_4_later_5_left));  // open: subed
  sub_4_later sub_4_later_6 (
    .\new (1'b0), .subee(sub_4_later_5_left), .suber(B), .left(sub_4_later_6_left));  // open: subed
  sub_4_later sub_4_later_7 (.\new (1'b0), .subee(sub_4_later_6_left), .suber(B), .left(C[2:0]));  // open: subed

  assign C[10:3] = A;

  // Other names for the same wires on the sheet: ori[7:0] = A; suber[3:0] = B
endmodule

// F
module sub_4_first (
  input  [3:0] subee,
  input  [3:0] suber,
  output subed,
  output [2:0] left
);

  wire [3:0] xor_1_out;
  wire [3:3] multiplexer_1_out;

  assign xor_1_out = subee ^ suber;  // XOR_Gate xor_1, 4 bits wide
  Multiplexer #(.width(4), .enable("false")) multiplexer_1 (
    .in0(subee), .in1(xor_1_out), .out({multiplexer_1_out[3], left}), .sel(subee[3]));

  assign subed = subee[3];

  // Other names for the same wires on the sheet: high = subee[3]

  // Notes on the sheet:
  //   默认除数第一位必定为1
endmodule

// L
module sub_4_later (
  input  \new ,
  input  [2:0] subee,
  input  [3:0] suber,
  output subed,
  output [2:0] left
);

  wire [3:0] xor_1_out;
  wire [3:3] multiplexer_1_out;

  assign xor_1_out = {subee, \new } ^ suber;  // XOR_Gate xor_1, 4 bits wide
  Multiplexer #(.width(4), .enable("false")) multiplexer_1 (
    .in0({subee, \new }), .in1(xor_1_out), .out({multiplexer_1_out[3], left}), .sel(subee[2]));

  assign subed = subee[2];

  // Other names for the same wires on the sheet: high = subee[2]

  // Notes on the sheet:
  //   默认除数第一位必定为1
endmodule
