// Logisim project GRF(封装式).circ as structural Verilog: 2 circuits, main circuit grf
module grf (
  input  clk,
  input  reset,
  input  WE,
  input  [4:0] A1,
  input  [4:0] A2,
  input  [4:0] A3,
  input  [31:0] WD,
  output [31:0] RD1,
  output [31:0] RD2
);

  wire demultiplexer_1_out0, demultiplexer_1_out1, demultiplexer_1_out2, demultiplexer_1_out3;
  wire [31:0] _0_7_rd1, _0_7_rd2, _8_15_rd1, _8_15_rd2, _16_23_rd1, _16_23_rd2, _24_31_rd1, _24_31_rd2;

  Demultiplexer #(.select(2)) demultiplexer_1 (
    .out0(demultiplexer_1_out0), .out1(demultiplexer_1_out1), .out2(demultiplexer_1_out2),
    .out3(demultiplexer_1_out3), .in(WE), .sel(A3[4:3]));  // open: en
  grf_8_unit _0_7 (
    .A1_0_to_3(A1[2:0]), .A2_0_to_3(A2[2:0]), .reset(reset), .A3_0_to_3(A3[2:0]), .RD1(_0_7_rd1),
    .RD2(_0_7_rd2), .clk(clk), .WD(WD), .WE(demultiplexer_1_out0), .zero_register(1'b1));
  grf_8_unit _8_15 (
    .A1_0_to_3(A1[2:0]), .A2_0_to_3(A2[2:0]), .reset(reset), .A3_0_to_3(A3[2:0]), .RD1(_8_15_rd1),
    .RD2(_8_15_rd2), .clk(clk), .WD(WD), .WE(demultiplexer_1_out1), .zero_register(1'b0));
  grf_8_unit _16_23 (
    .A1_0_to_3(A1[2:0]), .A2_0_to_3(A2[2:0]), .reset(reset), .A3_0_to_3(A3[2:0]), .RD1(_16_23_rd1),
    .RD2(_16_23_rd2), .clk(clk), .WD(WD), .WE(demultiplexer_1_out2), .zero_register(1'b0));
  grf_8_unit _24_31 (
    .A1_0_to_3(A1[2:0]), .A2_0_to_3(A2[2:0]), .reset(reset), .A3_0_to_3(A3[2:0]), .RD1(_24_31_rd1),
    .RD2(_24_31_rd2), .clk(clk), .WD(WD), .WE(demultiplexer_1_out3), .zero_register(1'b0));
  Multiplexer #(.select(2), .width(32), .disabled(0)) multiplexer_1 (
    .in0(_0_7_rd1), .in1(_8_15_rd1), .in2(_16_23_rd1), .in3(_24_31_rd1), .out(RD1), .sel(A1[4:3]));  // open: en
  Multiplexer #(.select(2), .width(32), .disabled(0)) multiplexer_2 (
    .in0(_0_7_rd2), .in1(_8_15_rd2), .in2(_16_23_rd2), .in3(_24_31_rd2), .out(RD2), .sel(A2[4:3]));  // open: en
endmodule

module grf_8_unit (
  input  [2:0] A1_0_to_3,
  input  [2:0] A2_0_to_3,
  input  zero_register,
  input  reset,
  input  clk,
  input  [31:0] WD,
  input  WE,
  input  [2:0] A3_0_to_3,
  output [31:0] RD1,
  output [31:0] RD2
);

  wire demultiplexer_1_out0, demultiplexer_1_out1, demultiplexer_1_out2, demultiplexer_1_out3,
       demultiplexer_1_out4, demultiplexer_1_out5, demultiplexer_1_out6, demultiplexer_1_out7;
  wire [31:0] _0_q, _1_q, _2_q, _3_q, _4_q, _5_q, _6_q, _7_q, multiplexer_1_out;

  Multiplexer #(.width(32), .disabled(0), .enable("false")) multiplexer_1 (
    .in0(WD), .in1({32{1'b0}}), .out(multiplexer_1_out), .sel(zero_register));
  Demultiplexer #(.select(3), .disabled(0)) demultiplexer_1 (
    .out0(demultiplexer_1_out0), .out1(demultiplexer_1_out1), .out2(demultiplexer_1_out2),
    .out3(demultiplexer_1_out3), .out4(demultiplexer_1_out4), .out5(demultiplexer_1_out5),
    .out6(demultiplexer_1_out6), .out7(demultiplexer_1_out7), .in(WE), .sel(A3_0_to_3));  // open: en
  Register #(.width(32)) _0 (.D(multiplexer_1_out), .en(demultiplexer_1_out0), .Q(_0_q), .clk(clk), .clr(reset));
  Register #(.width(32)) _1 (.D(WD), .en(demultiplexer_1_out1), .Q(_1_q), .clk(clk), .clr(reset));
  Register #(.width(32)) _2 (.D(WD), .en(demultiplexer_1_out2), .Q(_2_q), .clk(clk), .clr(reset));
  Register #(.width(32)) _3 (.D(WD), .en(demultiplexer_1_out3), .Q(_3_q), .clk(clk), .clr(reset));
  Register #(.width(32)) _4 (.D(WD), .en(demultiplexer_1_out4), .Q(_4_q), .clk(clk), .clr(reset));
  Register #(.width(32)) _5 (.D(WD), .en(demultiplexer_1_out5), .Q(_5_q), .clk(clk), .clr(reset));
  Register #(.width(32)) _6 (.D(WD), .en(demultiplexer_1_out6), .Q(_6_q), .clk(clk), .clr(reset));
  Register #(.width(32)) _7 (.D(WD), .en(demultiplexer_1_out7), .Q(_7_q), .clk(clk), .clr(reset));
  Multiplexer #(.select(3), .width(32), .disabled(0)) multiplexer_2 (
    .in0(_0_q), .in1(_1_q), .in2(_2_q), .in3(_3_q), .in4(_4_q), .in5(_5_q), .in6(_6_q), .in7(_7_q),
    .out(RD1), .sel(A1_0_to_3));  // open: en
  Multiplexer #(.select(3), .width(32), .disabled(0)) multiplexer_3 (
    .in0(_0_q), .in1(_1_q), .in2(_2_q), .in3(_3_q), .in4(_4_q), .in5(_5_q), .in6(_6_q), .in7(_7_q),
    .out(RD2), .sel(A2_0_to_3));  // open: en
endmodule
