// Logisim project alu_4bit_串行.circ as structural Verilog: 3 circuits, main circuit alu
module alu (
  input  [1:0] operation,
  input  [3:0] A,
  input  [3:0] B,
  output [3:0] C
);

  wire alu_1_bit_1_cout, alu_1_bit_2_cout, alu_1_bit_3_cout, comparator_1_eq;

  Comparator #(.width(2), .mode("unsigned")) comparator_1 (
    .a(operation), .b(2'b01), .eq(comparator_1_eq));  // open: gt, lt
  alu_1_bit alu_1_bit_1 (
    .operation(operation), .A(A[0]), .B(B[0]), .Cin(comparator_1_eq), .Cout(alu_1_bit_1_cout), .S(C[0]));
  alu_1_bit alu_1_bit_2 (
    .operation(operation), .A(A[1]), .B(B[1]), .Cin(alu_1_bit_1_cout), .Cout(alu_1_bit_2_cout), .S(C[1]));
  alu_1_bit alu_1_bit_3 (
    .operation(operation), .A(A[2]), .B(B[2]), .Cin(alu_1_bit_2_cout), .Cout(alu_1_bit_3_cout), .S(C[2]));
  alu_1_bit alu_1_bit_4 (.operation(operation), .A(A[3]), .B(B[3]), .Cin(alu_1_bit_3_cout), .S(C[3]));  // open: Cout
endmodule

// 0
module alu_1_bit (
  input  [1:0] operation,
  input  A,
  input  B,
  input  Cin,
  output S,
  output Cout
);

  wire adder_1_cout, adder_1_s, adder_2_cout, adder_2_s, and_1_out, not_1_out, not_2_out, not_3_out, or_1_out;

  not not_1 (not_1_out, A);
  not not_2 (not_2_out, B);
  not not_3 (not_3_out, Cin);
  adder adder_1 (.A(A), .B(B), .Cin(Cin), .S(adder_1_s), .Cout(adder_1_cout));
  Multiplexer #(.select(2), .disabled(0)) multiplexer_1 (
    .in0(adder_1_cout), .in1(adder_2_cout), .out(Cout), .sel(operation));  // open: in2, in3, en
  Pull_Resistor pull_resistor_1 (.node(Cout));
  adder adder_2 (.A(A), .B(not_2_out), .Cin(Cin), .S(adder_2_s), .Cout(adder_2_cout));
  and and_1 (and_1_out, B, A);
  or or_1 (or_1_out, B, A);
  Multiplexer #(.select(2)) multiplexer_2 (
    .in0(adder_1_s), .in1(adder_2_s), .in2(and_1_out), .in3(or_1_out), .out(S), .sel(operation));  // open: en

  // Other names for the same wires on the sheet: operator_tunnel[1:0] = operation
endmodule

module adder (
  input  A,
  input  B,
  input  Cin,
  output S,
  output Cout
);

  wire and_1_out, and_2_out, and_3_out, or_1_out, xor_1_out;

  xor xor_1 (xor_1_out, A, B);
  and and_1 (and_1_out, A, B);
  and and_2 (and_2_out, A, Cin);
  xor xor_2 (S, xor_1_out, Cin);
  or or_1 (or_1_out, and_1_out, and_2_out);
  and and_3 (and_3_out, B, Cin);
  or or_2 (Cout, or_1_out, and_3_out);
endmodule
