// Logisim project alu_4bit_并行.circ as structural Verilog: 6 circuits, main circuit alu
module alu (
  input  [1:0] operation,
  input  [3:0] A,
  input  [3:0] B,
  output [3:0] C
);

  wire advance_1_1_c1, advance_2_1_c2, advance_3_1_c3, comparator_1_eq;

  Comparator #(.width(2), .mode("unsigned")) comparator_1 (
    .a(operation), .b(2'b01), .eq(comparator_1_eq));  // open: gt, lt
  alu_1_bit _0 (.operation(operation), .A(A[0]), .B(B[0]), .Cin(comparator_1_eq), .S(C[0]));  // open: Cout
  advance_1 advance_1_1 (.sub(comparator_1_eq), .C0(comparator_1_eq), .A0(A[0]), .B0(B[0]), .C1(advance_1_1_c1));
  alu_1_bit _1 (.operation(operation), .A(A[1]), .B(B[1]), .Cin(advance_1_1_c1), .S(C[1]));  // open: Cout
  advance_2 advance_2_1 (
    .sub(comparator_1_eq), .C0(comparator_1_eq), .A0(A[0]), .B0(B[0]), .A1(A[1]), .B1(B[1]),
    .C2(advance_2_1_c2));
  alu_1_bit _2 (.operation(operation), .A(A[2]), .B(B[2]), .Cin(advance_2_1_c2), .S(C[2]));  // open: Cout
  advance_3 advance_3_1 (
    .sub(comparator_1_eq), .C0(comparator_1_eq), .A0(A[0]), .B0(B[0]), .A1(A[1]), .B1(B[1]), .A2(A[2]),
    .B2(B[2]), .C3(advance_3_1_c3));
  alu_1_bit _3 (.operation(operation), .A(A[3]), .B(B[3]), .Cin(advance_3_1_c3), .S(C[3]));  // open: Cout

  // Notes on the sheet:
  //   对于超前进位法实现ALU，注意减法的进位计算算法不同于加法。
endmodule

module alu_1_bit (
  input  [1:0] operation,
  input  A,
  input  B,
  input  Cin,
  output Cout,
  output S
);

  wire adder_1_cout, adder_1_s, adder_2_cout, adder_2_s, and_1_out, not_1_out, not_2_out, not_3_out, or_1_out;

  not not_1 (not_1_out, A);
  not not_2 (not_2_out, B);
  not not_3 (not_3_out, Cin);
  adder adder_1 (.A(A), .B(B), .Cin(Cin), .S(adder_1_s), .Cout(adder_1_cout));
  Multiplexer #(.select(2)) multiplexer_1 (
    .in0(adder_1_cout), .in1(adder_2_cout), .out(Cout), .sel(operation));  // open: in2, in3, en
  adder adder_2 (.A(A), .B(not_2_out), .Cin(Cin), .S(adder_2_s), .Cout(adder_2_cout));
  and and_1 (and_1_out, B, A);
  or or_1 (or_1_out, B, A);
  Multiplexer #(.select(2)) multiplexer_2 (
    .in0(adder_1_s), .in1(adder_2_s), .in2(and_1_out), .in3(or_1_out), .out(S), .sel(operation));  // open: en

  // Other names for the same wires on the sheet: operator_tunnel[1:0] = operation
endmodule

module adder (
  input  A,
  input  B,
  input  Cin,
  output S,
  output Cout
);

  wire and_1_out, and_2_out, and_3_out;

  xor odd_parity_1 (S, A, B, Cin);
  and and_1 (and_1_out, A, B);
  and and_2 (and_2_out, A, Cin);
  and and_3 (and_3_out, B, Cin);
  or or_1 (Cout, and_1_out, and_2_out, and_3_out);
endmodule

module advance_1 (
  input  sub,
  input  C0,
  input  A0,
  input  B0,
  output C1
);

  wire and_1_out, and_2_out, multiplexer_1_out, not_1_out, xor_1_out;

  Multiplexer multiplexer_1 (.in0(B0), .in1(not_1_out), .out(multiplexer_1_out), .sel(sub));  // open: en
  not not_1 (not_1_out, B0);
  xor xor_1 (xor_1_out, A0, multiplexer_1_out);
  and and_1 (and_1_out, A0, multiplexer_1_out);
  and and_2 (and_2_out, xor_1_out, C0);
  or or_1 (C1, and_1_out, and_2_out);
endmodule

module advance_2 (
  input  sub,
  input  C0,
  input  A0,
  input  B0,
  input  A1,
  input  B1,
  output C2
);

  wire and_1_out, and_2_out, and_3_out, multiplexer_1_out, multiplexer_2_out, not_1_out, not_2_out,
       xor_1_out, xor_2_out, xor_3_out;

  Multiplexer multiplexer_1 (.in0(B0), .in1(not_1_out), .out(multiplexer_1_out), .sel(sub));  // open: en
  not not_1 (not_1_out, B0);
  Multiplexer multiplexer_2 (.in0(B1), .in1(not_2_out), .out(multiplexer_2_out), .sel(sub));  // open: en
  not not_2 (not_2_out, B1);
  xor xor_1 (xor_1_out, A1, multiplexer_2_out);
  xor xor_2 (xor_2_out, A1, multiplexer_2_out);
  xor xor_3 (xor_3_out, A0, multiplexer_1_out);
  and and_1 (and_1_out, A1, multiplexer_2_out);
  and and_2 (and_2_out, A0, multiplexer_1_out, xor_1_out);
  and and_3 (and_3_out, xor_2_out, xor_3_out, C0);
  or or_1 (C2, and_1_out, and_2_out, and_3_out);
endmodule

module advance_3 (
  input  sub,
  input  C0,
  input  A0,
  input  B0,
  input  A1,
  input  B1,
  input  A2,
  input  B2,
  output C3
);

  wire and_1_out, and_2_out, and_3_out, and_4_out, multiplexer_1_out, multiplexer_2_out, multiplexer_3_out,
       not_1_out, not_2_out, not_3_out, xor_1_out, xor_2_out, xor_3_out, xor_4_out, xor_5_out, xor_6_out;

  not not_1 (not_1_out, B0);
  not not_2 (not_2_out, B1);
  not not_3 (not_3_out, B2);
  Multiplexer multiplexer_1 (.in0(B0), .in1(not_1_out), .out(multiplexer_1_out), .sel(sub));  // open: en
  Multiplexer multiplexer_2 (.in0(B1), .in1(not_2_out), .out(multiplexer_2_out), .sel(sub));  // open: en
  Multiplexer multiplexer_3 (.in0(B2), .in1(not_3_out), .out(multiplexer_3_out), .sel(sub));  // open: en
  xor xor_1 (xor_1_out, A2, multiplexer_3_out);
  xor xor_2 (xor_2_out, A2, multiplexer_3_out);
  xor xor_3 (xor_3_out, A1, multiplexer_2_out);
  xor xor_4 (xor_4_out, A2, multiplexer_3_out);
  xor xor_5 (xor_5_out, A1, multiplexer_2_out);
  xor xor_6 (xor_6_out, A0, multiplexer_1_out);
  and and_1 (and_1_out, A2, multiplexer_3_out);
  and and_2 (and_2_out, A1, multiplexer_2_out, xor_1_out);
  and and_3 (and_3_out, xor_2_out, xor_3_out, A0, multiplexer_1_out);
  and and_4 (and_4_out, xor_4_out, xor_5_out, xor_6_out, C0);
  or or_1 (C3, and_1_out, and_2_out, and_3_out, and_4_out);
endmodule
