// Logisim project fsm.circ as structural Verilog: 3 circuits, main circuit fsm
module fsm (
  input  Reset,
  input  [1:0] In,
  output Z
);

  wire clock_1_out;
  wire [1:0] multiplexer_1_out, staet_res_q, state_1_out_3;

  state state_1 (.S(staet_res_q), .I(In), .out_3(state_1_out_3));
  // Probe on multiplexer_1_out
  Multiplexer #(.width(2), .enable("false")) multiplexer_1 (
    .in0(state_1_out_3), .in1(2'b00), .out(multiplexer_1_out), .sel(Reset));
  Register #(.width(2)) staet_res (.D(multiplexer_1_out), .Q(staet_res_q), .clk(clock_1_out));  // open: en, clr
  Clock clock_1 (.out(clock_1_out));
  \output  output_1 (.S(staet_res_q), .Input(In), .Out(Z));
endmodule

module state (
  input  [1:0] S,
  input  [1:0] I,
  output [1:0] out_3
);

  wire not_1_out, not_2_out;

  not not_1 (not_1_out, I[0]);
  not not_2 (not_2_out, I[1]);
  and and_1 (out_3[1], S[0], not_1_out);
  and and_2 (out_3[0], not_2_out, I[0]);
endmodule

module \output  (
  input  [1:0] S,
  input  [1:0] Input,
  output Out
);

  wire not_1_out;

  not not_1 (not_1_out, Input[0]);
  and and_1 (Out, S[1], not_1_out);
endmodule
