// Logisim project GRF(32位并行式).circ as structural Verilog: 1 circuit, main circuit grf
module grf (
  input  clk,
  input  reset,
  input  WE,
  input  [31:0] WD,
  input  [4:0] A1,
  input  [4:0] A2,
  input  [4:0] A3,
  output [31:0] RD1,
  output [31:0] RD2
);

  wire en_0, en_1, en_2, en_3, en_4, en_5, en_6, en_7, en_8, en_9, en_10, en_11, en_12, en_13, en_14, en_15,
       en_16, en_17, en_18, en_19, en_20, en_21, en_22, en_23, en_24, en_25, en_26, en_27, en_28, en_29,
       en_30, en_31;
  wire [31:0] data_0, data_1, data_2, data_3, data_4, data_5, data_6, data_7, data_8, data_9, data_10,
       data_11, data_12, data_13, data_14, data_15, data_16, data_17, data_18, data_19, data_20, data_21,
       data_22, data_23, data_24, data_25, data_26, data_27, data_28, data_29, data_30, data_31, output_0,
       output_1, output_2, output_3, output_4, output_5, output_6, output_7, output_8, output_9, output_10,
       output_11, output_12, output_13, output_14, output_15, output_16, output_17, output_18, output_19,
       output_20, output_21, output_22, output_23, output_24, output_25, output_26, output_27, output_28,
       output_29, output_30, output_31;

  Demultiplexer #(.select(5), .width(32), .tristate("true")) demultiplexer_1 (
    .out0(data_0), .out1(data_1), .out2(data_2), .out3(data_3), .out4(data_4), .out5(data_5), .out6(data_6),
    .out7(data_7), .out8(data_8), .out9(data_9), .out10(data_10), .out11(data_11), .out12(data_12),
    .out13(data_13), .out14(data_14), .out15(data_15), .out16(data_16), .out17(data_17), .out18(data_18),
    .out19(data_19), .out20(data_20), .out21(data_21), .out22(data_22), .out23(data_23), .out24(data_24),
    .out25(data_25), .out26(data_26), .out27(data_27), .out28(data_28), .out29(data_29), .out30(data_30),
    .out31(data_31), .in(WD), .sel(A3), .en(WE));
  Decoder #(.select(5), .disabled(0)) decoder_1 (
    .out0(en_0), .out1(en_1), .out2(en_2), .out3(en_3), .out4(en_4), .out5(en_5), .out6(en_6), .out7(en_7),
    .out8(en_8), .out9(en_9), .out10(en_10), .out11(en_11), .out12(en_12), .out13(en_13), .out14(en_14),
    .out15(en_15), .out16(en_16), .out17(en_17), .out18(en_18), .out19(en_19), .out20(en_20), .out21(en_21),
    .out22(en_22), .out23(en_23), .out24(en_24), .out25(en_25), .out26(en_26), .out27(en_27), .out28(en_28),
    .out29(en_29), .out30(en_30), .out31(en_31), .sel(A3), .en(WE));
  Register #(.width(32)) _0 (.D(data_0), .en(1'b0), .Q(output_0), .clk(clk), .clr(reset));
  Register #(.width(32)) _8 (.D(data_8), .en(en_8), .Q(output_8), .clk(clk), .clr(reset));
  Register #(.width(32)) _16 (.D(data_16), .en(en_16), .Q(output_16), .clk(clk), .clr(reset));
  Register #(.width(32)) _24 (.D(data_24), .en(en_24), .Q(output_24), .clk(clk), .clr(reset));
  Register #(.width(32)) _1 (.D(data_1), .en(en_1), .Q(output_1), .clk(clk), .clr(reset));
  Register #(.width(32)) _9 (.D(data_9), .en(en_9), .Q(output_9), .clk(clk), .clr(reset));
  Register #(.width(32)) _17 (.D(data_17), .en(en_17), .Q(output_17), .clk(clk), .clr(reset));
  Register #(.width(32)) _25 (.D(data_25), .en(en_25), .Q(output_25), .clk(clk), .clr(reset));
  Register #(.width(32)) _2 (.D(data_2), .en(en_2), .Q(output_2), .clk(clk), .clr(reset));
  Register #(.width(32)) _10 (.D(data_10), .en(en_10), .Q(output_10), .clk(clk), .clr(reset));
  Register #(.width(32)) _18 (.D(data_18), .en(en_18), .Q(output_18), .clk(clk), .clr(reset));
  Register #(.width(32)) _26 (.D(data_26), .en(en_26), .Q(output_26), .clk(clk), .clr(reset));
  Register #(.width(32)) _3 (.D(data_3), .en(en_3), .Q(output_3), .clk(clk), .clr(reset));
  Register #(.width(32)) _11 (.D(data_11), .en(en_11), .Q(output_11), .clk(clk), .clr(reset));
  Register #(.width(32)) _19 (.D(data_19), .en(en_19), .Q(output_19), .clk(clk), .clr(reset));
  Register #(.width(32)) _27 (.D(data_27), .en(en_27), .Q(output_27), .clk(clk), .clr(reset));
  Register #(.width(32)) _4 (.D(data_4), .en(en_4), .Q(output_4), .clk(clk), .clr(reset));
  Register #(.width(32)) _12 (.D(data_12), .en(en_12), .Q(output_12), .clk(clk), .clr(reset));
  Register #(.width(32)) _20 (.D(data_20), .en(en_20), .Q(output_20), .clk(clk), .clr(reset));
  Register #(.width(32)) _28 (.D(data_28), .en(en_28), .Q(output_28), .clk(clk), .clr(reset));
  Register #(.width(32)) _5 (.D(data_5), .en(en_5), .Q(output_5), .clk(clk), .clr(reset));
  Register #(.width(32)) _13 (.D(data_13), .en(en_13), .Q(output_13), .clk(clk), .clr(reset));
  Register #(.width(32)) _21 (.D(data_21), .en(en_21), .Q(output_21), .clk(clk), .clr(reset));
  Register #(.width(32)) _29 (.D(data_29), .en(en_29), .Q(output_29), .clk(clk), .clr(reset));
  Register #(.width(32)) _6 (.D(data_6), .en(en_6), .Q(output_6), .clk(clk), .clr(reset));
  Register #(.width(32)) _14 (.D(data_14), .en(en_14), .Q(output_14), .clk(clk), .clr(reset));
  Register #(.width(32)) _22 (.D(data_22), .en(en_22), .Q(output_22), .clk(clk), .clr(reset));
  Register #(.width(32)) _30 (.D(data_30), .en(en_30), .Q(output_30), .clk(clk), .clr(reset));
  Register #(.width(32)) _7 (.D(data_7), .en(en_7), .Q(output_7), .clk(clk), .clr(reset));
  Register #(.width(32)) _15 (.D(data_15), .en(en_15), .Q(output_15), .clk(clk), .clr(reset));
  Register #(.width(32)) _23 (.D(data_23), .en(en_23), .Q(output_23), .clk(clk), .clr(reset));
  Register #(.width(32)) _31 (.D(data_31), .en(en_31), .Q(output_31), .clk(clk), .clr(reset));
  Multiplexer #(.select(5), .width(32)) multiplexer_1 (
    .in0(output_0), .in1(output_1), .in2(output_2), .in3(output_3), .in4(output_4), .in5(output_5),
    .in6(output_6), .in7(output_7), .in8(output_8), .in9(output_9), .in10(output_10), .in11(output_11),
    .in12(output_12), .in13(output_13), .in14(output_14), .in15(output_15), .in16(output_16),
    .in17(output_17), .in18(output_18), .in19(output_19), .in20(output_20), .in21(output_21),
    .in22(output_22), .in23(output_23), .in24(output_24), .in25(output_25), .in26(output_26),
    .in27(output_27), .in28(output_28), .in29(output_29), .in30(output_30), .in31(output_31), .out(RD1),
    .sel(A1));  // open: en
  Multiplexer #(.select(5), .width(32)) multiplexer_2 (
    .in0(output_0), .in1(output_1), .in2(output_2), .in3(output_3), .in4(output_4), .in5(output_5),
    .in6(output_6), .in7(output_7), .in8(output_8), .in9(output_9), .in10(output_10), .in11(output_11),
    .in12(output_12), .in13(output_13), .in14(output_14), .in15(output_15), .in16(output_16),
    .in17(output_17), .in18(output_18), .in19(output_19), .in20(output_20), .in21(output_21),
    .in22(output_22), .in23(output_23), .in24(output_24), .in25(output_25), .in26(output_26),
    .in27(output_27), .in28(output_28), .in29(output_29), .in30(output_30), .in31(output_31), .out(RD2),
    .sel(A2));  // open: en

  // Notes on the sheet:
  //   Chinese is not recommended
  //   With double security methods : WD to certain reg and WE to certain reg
endmodule
