// Logisim project p3_version2 - final submission.circ as structural Verilog: 12 circuits, main circuit GRF
module main (
  input  Reset,
  output [31:0] Instr,
  output RegWrite,
  output [4:0] RegAddr,
  output [31:0] RegData,
  output MemWrite,
  output [4:0] MemAddr,
  output [31:0] Memdata
);

  wire alu_1_aluzero, AluSrc, Clock, ExtOp, MemRead, MemToReg, PcBranch, RegDst;
  wire [2:0] AluOp, controller_1_aluctrl;
  wire [4:0] if_1_instr_15_11, if_1_instr_20_16, if_1_instr_25_21, IF_10_6;
  wire [5:0] IF_5_0, IF_31_26;
  wire [15:0] if_1_instr_15_0;
  wire [31:0] BranchResult, extender_1_out, grf_1_rd1, if_1_pc_4, memory_1_out_7, multiplexer_3_out,
       nadd_1_out_3, OUT_MemAddr32;

  Clock clock_1 (.out(Clock));
  // Probe on Instr
  IF if_1 (
    .BranchResult(BranchResult), .BranchInstr(PcBranch), .Instr(Instr), .Instr_31_26(IF_31_26),
    .Instr_25_21(if_1_instr_25_21), .Instr_20_16(if_1_instr_20_16), .Instr_15_11(if_1_instr_15_11),
    .Instr_10_6(IF_10_6), .Instr_5_0(IF_5_0), .Instr_15_0(if_1_instr_15_0), .clk(Clock), .Reset(Reset),
    .PC_4(if_1_pc_4));  // open: Instr_25_0
  Multiplexer #(.width(5), .enable("false")) multiplexer_1 (
    .in0(if_1_instr_20_16), .in1(if_1_instr_15_11), .out(RegAddr), .sel(RegDst));
  Multiplexer #(.width(32), .enable("false")) multiplexer_2 (
    .in0({OUT_MemAddr32[31:7], MemAddr, OUT_MemAddr32[1:0]}), .in1(memory_1_out_7), .out(RegData),
    .sel(MemToReg));
  Controller controller_1 (
    .Op(IF_31_26), .RegWrite(RegWrite), .MemRead(MemRead), .MemWrite(MemWrite), .AluSrc_R2_Im(AluSrc),
    .PcBranch(PcBranch), .RegDst(RegDst), .MemToReg(MemToReg), .ExtOp(ExtOp), .AluCtrl(controller_1_aluctrl));  // open: Jump_sel
  Extender extender_1 (.ExtOp(ExtOp), .Input(if_1_instr_15_0), .Out(extender_1_out));
  GRF grf_1 (
    .clk(Clock), .reset(Reset), .WE(RegWrite), .WD(RegData), .A1(if_1_instr_25_21), .A2(if_1_instr_20_16),
    .A3(RegAddr), .RD1(grf_1_rd1), .RD2(Memdata));
  // Probe on controller_1_aluctrl
  AluController alucontroller_1 (.AluCtrl(controller_1_aluctrl), .Function(IF_5_0), .out_3(AluOp));
  // Probe on AluOp
  Nadd nadd_1 (.Offset_ext(extender_1_out), .PC_4(if_1_pc_4), .out_3(nadd_1_out_3));
  Multiplexer #(.width(32), .enable("false")) multiplexer_3 (
    .in0(Memdata), .in1(extender_1_out), .out(multiplexer_3_out), .sel(AluSrc));
  ALU alu_1 (
    .A(grf_1_rd1), .B(multiplexer_3_out), .AluOp(AluOp), .AluZero(alu_1_aluzero),
    .AluOut({OUT_MemAddr32[31:7], MemAddr, OUT_MemAddr32[1:0]}), .C(IF_10_6));
  Multiplexer #(.width(32), .enable("false")) multiplexer_4 (
    .in0(if_1_pc_4), .in1(nadd_1_out_3), .out(BranchResult), .sel(alu_1_aluzero));
  Memory memory_1 (
    .Addr({OUT_MemAddr32[31:7], MemAddr, OUT_MemAddr32[1:0]}), .WriteData(Memdata), .MemWrite(MemWrite),
    .Clock(Clock), .MemRead(MemRead), .Reset(Reset), .out_7(memory_1_out_7));

  // Other names for the same wires on the sheet: OUT_Instr[31:0] = Instr; OUT_MemAddr32[6:2] = MemAddr;
  //   OUT_MemData[31:0] = Memdata; OUT_MemWrite = MemWrite; OUT_RegAddr[4:0] = RegAddr; OUT_RegData[31:0] = RegData;
  //   OUT_RegWrite = RegWrite

  // Notes on the sheet:
  //   input
endmodule

module main_label (
  input  Reset,
  output [31:0] Instr,
  output RegWrite,
  output [4:0] RegAddr,
  output [31:0] RegData,
  output MemWrite,
  output [4:0] MemAddr,
  output [31:0] Memdata
);

  wire alu_1_aluzero, AluSrc, Clock, ExtOp, MemRead, MemToReg, PcBranch, RegDst;
  wire [2:0] AluOp, controller_1_aluctrl;
  wire [4:0] if_1_instr_15_11, if_1_instr_20_16, if_1_instr_25_21, IF_10_6;
  wire [5:0] IF_5_0, IF_31_26;
  wire [15:0] IF_15_0;
  wire [31:0] ALUResult, BranchResult, Ext32, grf_1_rd1, if_1_pc_4, MemReadData, multiplexer_3_out,
       nadd_1_out_3;

  Clock clock_1 (.out(Clock));
  // Probe on Instr
  IF if_1 (
    .BranchResult(BranchResult), .BranchInstr(PcBranch), .Instr(Instr), .Instr_31_26(IF_31_26),
    .Instr_25_21(if_1_instr_25_21), .Instr_20_16(if_1_instr_20_16), .Instr_15_11(if_1_instr_15_11),
    .Instr_10_6(IF_10_6), .Instr_5_0(IF_5_0), .Instr_15_0(IF_15_0), .clk(Clock), .Reset(Reset),
    .PC_4(if_1_pc_4));  // open: Instr_25_0
  Multiplexer #(.width(5), .enable("false")) multiplexer_1 (
    .in0(if_1_instr_20_16), .in1(if_1_instr_15_11), .out(RegAddr), .sel(RegDst));
  Multiplexer #(.width(32), .enable("false")) multiplexer_2 (
    .in0({ALUResult[31:7], MemAddr, ALUResult[1:0]}), .in1(MemReadData), .out(RegData), .sel(MemToReg));
  Controller controller_1 (
    .Op(IF_31_26), .RegWrite(RegWrite), .MemRead(MemRead), .MemWrite(MemWrite), .AluSrc_R2_Im(AluSrc),
    .PcBranch(PcBranch), .RegDst(RegDst), .MemToReg(MemToReg), .ExtOp(ExtOp), .AluCtrl(controller_1_aluctrl));  // open: Jump_sel
  GRF grf_1 (
    .clk(Clock), .reset(Reset), .WE(RegWrite), .WD(RegData), .A1(if_1_instr_25_21), .A2(if_1_instr_20_16),
    .A3(RegAddr), .RD1(grf_1_rd1), .RD2(Memdata));
  Extender extender_1 (.ExtOp(ExtOp), .Input(IF_15_0), .Out(Ext32));
  // Probe on controller_1_aluctrl
  // Probe on AluOp
  AluController alucontroller_1 (.AluCtrl(controller_1_aluctrl), .Function(IF_5_0), .out_3(AluOp));
  Nadd nadd_1 (.Offset_ext(Ext32), .PC_4(if_1_pc_4), .out_3(nadd_1_out_3));
  Multiplexer #(.width(32), .enable("false")) multiplexer_3 (
    .in0(Memdata), .in1(Ext32), .out(multiplexer_3_out), .sel(AluSrc));
  ALU alu_1 (
    .A(grf_1_rd1), .B(multiplexer_3_out), .AluOp(AluOp), .AluZero(alu_1_aluzero),
    .AluOut({ALUResult[31:7], MemAddr, ALUResult[1:0]}), .C(IF_10_6));
  Multiplexer #(.width(32), .enable("false")) multiplexer_4 (
    .in0(if_1_pc_4), .in1(nadd_1_out_3), .out(BranchResult), .sel(alu_1_aluzero));
  Memory memory_1 (
    .Addr({ALUResult[31:7], MemAddr, ALUResult[1:0]}), .WriteData(Memdata), .MemWrite(MemWrite),
    .Clock(Clock), .MemRead(MemRead), .Reset(Reset), .out_7(MemReadData));

  // Other names for the same wires on the sheet: OUT_Instr[31:0] = Instr;
  //   OUT_MemAddr32[31:0] = {ALUResult[31:7], MemAddr, ALUResult[1:0]}; ALUResult[6:2] = MemAddr;
  //   OUT_MemWrite = MemWrite; OUT_RegAddr[4:0] = RegAddr; OUT_RegData[31:0] = RegData; OUT_RegWrite = RegWrite;
  //   OUT_MemData[31:0] = Memdata; RegData2[31:0] = Memdata

  // Notes on the sheet:
  //   input
endmodule

module main_v3_j (
  input  Reset,
  output [31:0] Instr,
  output RegWrite,
  output [4:0] RegAddr,
  output [31:0] RegData,
  output MemWrite,
  output [4:0] MemAddr,
  output [31:0] Memdata
);

  wire alu_1_aluzero, AluSrc, Clock, ExtOp, JumpSel, MemRead, MemToReg, PcBranch_Jump, RegDst;
  wire [2:0] AluOp, controller_1_aluctrl;
  wire [4:0] if_1_instr_15_11, if_1_instr_20_16, if_1_instr_25_21, IF_10_6;
  wire [5:0] IF_5_0, IF_31_26;
  wire [15:0] if_1_instr_15_0;
  wire [25:0] IF_25_0;
  wire [31:0] BranchResult, extender_1_out, grf_1_rd1, if_1_pc_4, jump_v3_1_pc, memory_1_out_7,
       multiplexer_3_out, multiplexer_4_out, nadd_1_out_3, OUT_MemAddr32;

  Clock clock_1 (.out(Clock));
  // Probe on Instr
  IF if_1 (
    .BranchResult(BranchResult), .BranchInstr(PcBranch_Jump), .Instr(Instr), .Instr_31_26(IF_31_26),
    .Instr_25_21(if_1_instr_25_21), .Instr_20_16(if_1_instr_20_16), .Instr_15_11(if_1_instr_15_11),
    .Instr_10_6(IF_10_6), .Instr_5_0(IF_5_0), .Instr_15_0(if_1_instr_15_0), .clk(Clock), .Reset(Reset),
    .PC_4(if_1_pc_4), .Instr_25_0(IF_25_0));
  Multiplexer #(.width(5), .enable("false")) multiplexer_1 (
    .in0(if_1_instr_20_16), .in1(if_1_instr_15_11), .out(RegAddr), .sel(RegDst));
  Multiplexer #(.width(32), .enable("false")) multiplexer_2 (
    .in0({OUT_MemAddr32[31:7], MemAddr, OUT_MemAddr32[1:0]}), .in1(memory_1_out_7), .out(RegData),
    .sel(MemToReg));
  Controller controller_1 (
    .Op(IF_31_26), .RegWrite(RegWrite), .MemRead(MemRead), .MemWrite(MemWrite), .AluSrc_R2_Im(AluSrc),
    .PcBranch(PcBranch_Jump), .RegDst(RegDst), .MemToReg(MemToReg), .ExtOp(ExtOp),
    .AluCtrl(controller_1_aluctrl), .Jump_sel(JumpSel));
  Extender extender_1 (.ExtOp(ExtOp), .Input(if_1_instr_15_0), .Out(extender_1_out));
  GRF grf_1 (
    .clk(Clock), .reset(Reset), .WE(RegWrite), .WD(RegData), .A1(if_1_instr_25_21), .A2(if_1_instr_20_16),
    .A3(RegAddr), .RD1(grf_1_rd1), .RD2(Memdata));
  // Probe on controller_1_aluctrl
  AluController alucontroller_1 (.AluCtrl(controller_1_aluctrl), .Function(IF_5_0), .out_3(AluOp));
  // Probe on AluOp
  Nadd nadd_1 (.Offset_ext(extender_1_out), .PC_4(if_1_pc_4), .out_3(nadd_1_out_3));
  Multiplexer #(.width(32), .enable("false")) multiplexer_3 (
    .in0(Memdata), .in1(extender_1_out), .out(multiplexer_3_out), .sel(AluSrc));
  Jump_v3 jump_v3_1 (.PC_4(if_1_pc_4), .IF_25_0(IF_25_0), .PC(jump_v3_1_pc));
  ALU alu_1 (
    .A(grf_1_rd1), .B(multiplexer_3_out), .AluOp(AluOp), .AluZero(alu_1_aluzero),
    .AluOut({OUT_MemAddr32[31:7], MemAddr, OUT_MemAddr32[1:0]}), .C(IF_10_6));
  Multiplexer #(.width(32), .enable("false")) multiplexer_4 (
    .in0(if_1_pc_4), .in1(nadd_1_out_3), .out(multiplexer_4_out), .sel(alu_1_aluzero));
  Multiplexer #(.width(32), .enable("false")) multiplexer_5 (
    .in0(multiplexer_4_out), .in1(jump_v3_1_pc), .out(BranchResult), .sel(JumpSel));
  Memory memory_1 (
    .Addr({OUT_MemAddr32[31:7], MemAddr, OUT_MemAddr32[1:0]}), .WriteData(Memdata), .MemWrite(MemWrite),
    .Clock(Clock), .MemRead(MemRead), .Reset(Reset), .out_7(memory_1_out_7));

  // Other names for the same wires on the sheet: OUT_Instr[31:0] = Instr; OUT_MemAddr32[6:2] = MemAddr;
  //   OUT_MemData[31:0] = Memdata; OUT_MemWrite = MemWrite; OUT_RegAddr[4:0] = RegAddr; OUT_RegData[31:0] = RegData;
  //   OUT_RegWrite = RegWrite

  // Notes on the sheet:
  //   input
endmodule

module GRF (
  input  clk,
  input  reset,
  input  WE,
  input  [31:0] WD,
  input  [4:0] A1,
  input  [4:0] A2,
  input  [4:0] A3,
  output [31:0] RD1,
  output [31:0] RD2
);

  wire en_0, en_1, en_2, en_3, en_4, en_5, en_6, en_7, en_8, en_9, en_10, en_11, en_12, en_13, en_14, en_15,
       en_16, en_17, en_18, en_19, en_20, en_21, en_22, en_23, en_24, en_25, en_26, en_27, en_28, en_29,
       en_30, en_31;
  wire [31:0] data_0, data_1, data_2, data_3, data_4, data_5, data_6, data_7, data_8, data_9, data_10,
       data_11, data_12, data_13, data_14, data_15, data_16, data_17, data_18, data_19, data_20, data_21,
       data_22, data_23, data_24, data_25, data_26, data_27, data_28, data_29, data_30, data_31, output_0,
       output_1, output_2, output_3, output_4, output_5, output_6, output_7, output_8, output_9, output_10,
       output_11, output_12, output_13, output_14, output_15, output_16, output_17, output_18, output_19,
       output_20, output_21, output_22, output_23, output_24, output_25, output_26, output_27, output_28,
       output_29, output_30, output_31;

  Demultiplexer #(.select(5), .width(32), .tristate("true")) demultiplexer_1 (
    .out0(data_0), .out1(data_1), .out2(data_2), .out3(data_3), .out4(data_4), .out5(data_5), .out6(data_6),
    .out7(data_7), .out8(data_8), .out9(data_9), .out10(data_10), .out11(data_11), .out12(data_12),
    .out13(data_13), .out14(data_14), .out15(data_15), .out16(data_16), .out17(data_17), .out18(data_18),
    .out19(data_19), .out20(data_20), .out21(data_21), .out22(data_22), .out23(data_23), .out24(data_24),
    .out25(data_25), .out26(data_26), .out27(data_27), .out28(data_28), .out29(data_29), .out30(data_30),
    .out31(data_31), .in(WD), .sel(A3), .en(WE));
  Decoder #(.select(5), .disabled(0)) decoder_1 (
    .out0(en_0), .out1(en_1), .out2(en_2), .out3(en_3), .out4(en_4), .out5(en_5), .out6(en_6), .out7(en_7),
    .out8(en_8), .out9(en_9), .out10(en_10), .out11(en_11), .out12(en_12), .out13(en_13), .out14(en_14),
    .out15(en_15), .out16(en_16), .out17(en_17), .out18(en_18), .out19(en_19), .out20(en_20), .out21(en_21),
    .out22(en_22), .out23(en_23), .out24(en_24), .out25(en_25), .out26(en_26), .out27(en_27), .out28(en_28),
    .out29(en_29), .out30(en_30), .out31(en_31), .sel(A3), .en(WE));
  Register #(.width(32)) _0 (.D(data_0), .en(1'b0), .Q(output_0), .clk(clk), .clr(reset));
  Register #(.width(32)) _8 (.D(data_8), .en(en_8), .Q(output_8), .clk(clk), .clr(reset));
  Register #(.width(32)) _16 (.D(data_16), .en(en_16), .Q(output_16), .clk(clk), .clr(reset));
  Register #(.width(32)) _24 (.D(data_24), .en(en_24), .Q(output_24), .clk(clk), .clr(reset));
  Register #(.width(32)) _1 (.D(data_1), .en(en_1), .Q(output_1), .clk(clk), .clr(reset));
  Register #(.width(32)) _9 (.D(data_9), .en(en_9), .Q(output_9), .clk(clk), .clr(reset));
  Register #(.width(32)) _17 (.D(data_17), .en(en_17), .Q(output_17), .clk(clk), .clr(reset));
  Register #(.width(32)) _25 (.D(data_25), .en(en_25), .Q(output_25), .clk(clk), .clr(reset));
  Register #(.width(32)) _2 (.D(data_2), .en(en_2), .Q(output_2), .clk(clk), .clr(reset));
  Register #(.width(32)) _10 (.D(data_10), .en(en_10), .Q(output_10), .clk(clk), .clr(reset));
  Register #(.width(32)) _18 (.D(data_18), .en(en_18), .Q(output_18), .clk(clk), .clr(reset));
  Register #(.width(32)) _26 (.D(data_26), .en(en_26), .Q(output_26), .clk(clk), .clr(reset));
  Register #(.width(32)) _3 (.D(data_3), .en(en_3), .Q(output_3), .clk(clk), .clr(reset));
  Register #(.width(32)) _11 (.D(data_11), .en(en_11), .Q(output_11), .clk(clk), .clr(reset));
  Register #(.width(32)) _19 (.D(data_19), .en(en_19), .Q(output_19), .clk(clk), .clr(reset));
  Register #(.width(32)) _27 (.D(data_27), .en(en_27), .Q(output_27), .clk(clk), .clr(reset));
  Register #(.width(32)) _4 (.D(data_4), .en(en_4), .Q(output_4), .clk(clk), .clr(reset));
  Register #(.width(32)) _12 (.D(data_12), .en(en_12), .Q(output_12), .clk(clk), .clr(reset));
  Register #(.width(32)) _20 (.D(data_20), .en(en_20), .Q(output_20), .clk(clk), .clr(reset));
  Register #(.width(32)) _28 (.D(data_28), .en(en_28), .Q(output_28), .clk(clk), .clr(reset));
  Register #(.width(32)) _5 (.D(data_5), .en(en_5), .Q(output_5), .clk(clk), .clr(reset));
  Register #(.width(32)) _13 (.D(data_13), .en(en_13), .Q(output_13), .clk(clk), .clr(reset));
  Register #(.width(32)) _21 (.D(data_21), .en(en_21), .Q(output_21), .clk(clk), .clr(reset));
  Register #(.width(32)) _29 (.D(data_29), .en(en_29), .Q(output_29), .clk(clk), .clr(reset));
  Register #(.width(32)) _6 (.D(data_6), .en(en_6), .Q(output_6), .clk(clk), .clr(reset));
  Register #(.width(32)) _14 (.D(data_14), .en(en_14), .Q(output_14), .clk(clk), .clr(reset));
  Register #(.width(32)) _22 (.D(data_22), .en(en_22), .Q(output_22), .clk(clk), .clr(reset));
  Register #(.width(32)) _30 (.D(data_30), .en(en_30), .Q(output_30), .clk(clk), .clr(reset));
  Register #(.width(32)) _7 (.D(data_7), .en(en_7), .Q(output_7), .clk(clk), .clr(reset));
  Register #(.width(32)) _15 (.D(data_15), .en(en_15), .Q(output_15), .clk(clk), .clr(reset));
  Register #(.width(32)) _23 (.D(data_23), .en(en_23), .Q(output_23), .clk(clk), .clr(reset));
  Register #(.width(32)) _31 (.D(data_31), .en(en_31), .Q(output_31), .clk(clk), .clr(reset));
  Multiplexer #(.select(5), .width(32)) multiplexer_1 (
    .in0(output_0), .in1(output_1), .in2(output_2), .in3(output_3), .in4(output_4), .in5(output_5),
    .in6(output_6), .in7(output_7), .in8(output_8), .in9(output_9), .in10(output_10), .in11(output_11),
    .in12(output_12), .in13(output_13), .in14(output_14), .in15(output_15), .in16(output_16),
    .in17(output_17), .in18(output_18), .in19(output_19), .in20(output_20), .in21(output_21),
    .in22(output_22), .in23(output_23), .in24(output_24), .in25(output_25), .in26(output_26),
    .in27(output_27), .in28(output_28), .in29(output_29), .in30(output_30), .in31(output_31), .out(RD1),
    .sel(A1));  // open: en
  Multiplexer #(.select(5), .width(32)) multiplexer_2 (
    .in0(output_0), .in1(output_1), .in2(output_2), .in3(output_3), .in4(output_4), .in5(output_5),
    .in6(output_6), .in7(output_7), .in8(output_8), .in9(output_9), .in10(output_10), .in11(output_11),
    .in12(output_12), .in13(output_13), .in14(output_14), .in15(output_15), .in16(output_16),
    .in17(output_17), .in18(output_18), .in19(output_19), .in20(output_20), .in21(output_21),
    .in22(output_22), .in23(output_23), .in24(output_24), .in25(output_25), .in26(output_26),
    .in27(output_27), .in28(output_28), .in29(output_29), .in30(output_30), .in31(output_31), .out(RD2),
    .sel(A2));  // open: en

  // Notes on the sheet:
  //   Chinese is not recommended
  //   With double security methods : WD to certain reg and WE to certain reg
endmodule

module IF (
  input  [31:0] BranchResult,
  input  BranchInstr,
  input  clk,
  input  Reset,
  output [31:0] PC_4,
  output [31:0] Instr,
  output [5:0] Instr_31_26,
  output [4:0] Instr_25_21,
  output [4:0] Instr_20_16,
  output [4:0] Instr_15_11,
  output [4:0] Instr_10_6,
  output [5:0] Instr_5_0,
  output [15:0] Instr_15_0,
  output [25:0] Instr_25_0
);

  wire comparator_1_eq, not_1_out;
  wire [31:0] divider_1_out, multiplexer_1_out, PC_q;

  Adder #(.width(32)) adder_1 (.a(PC_q), .b(32'h4), .out(PC_4));  // open: cin, cout
  Multiplexer #(.width(32), .enable("false")) multiplexer_1 (
    .in0(PC_4), .in1(BranchResult), .out(multiplexer_1_out), .sel(BranchInstr));
  Register #(.width(32)) PC (.D(multiplexer_1_out), .en(not_1_out), .Q(PC_q), .clk(clk), .clr(Reset));
  not not_1 (not_1_out, comparator_1_eq);
  Divider #(.width(32)) divider_1 (.a(PC_q), .b(32'h4), .out(divider_1_out));  // open: upper, rem
  Comparator #(.width(5), .mode("unsigned")) comparator_1 (
    .a(multiplexer_1_out[6:2]), .b({5{1'b0}}), .eq(comparator_1_eq));  // open: gt, lt
  ROM #(.addrWidth(5), .dataWidth(32)) rom_1 (.addr(divider_1_out[4:0]), .data(Instr));  // open: sel

  assign Instr_5_0 = Instr[5:0];
  assign Instr_10_6 = Instr[10:6];
  assign Instr_15_0 = Instr[15:0];
  assign Instr_15_11 = Instr[15:11];
  assign Instr_20_16 = Instr[20:16];
  assign Instr_25_0 = Instr[25:0];
  assign Instr_25_21 = Instr[25:21];
  assign Instr_31_26 = Instr[31:26];

  // Notes on the sheet:
  //   memory中的内容是按照字单位来存的，因此要在原地址上除以4
  //   在branch、jump指令中，请注意pc的值跳转是在已经+4的情况下考虑的。
  //   时钟越界时，必须停下来，否则会重新开始执行,当心最后一句跳转是否可行
  //   contents of rom_1 (hex, n*v repeats v):
  //   3c08ffff 3508ffff 3529000f 354a0010 356b0074 358c0064 86880 112a0004 0 ad680000 ad690004 ad6a0008
  //   ad6bfffc ad6cfff8 ad6dfff4 18a7021 11cb0004 0 8d900010 8d910014 8d920018 8d93000c 8d940008 8d950004
  //   7*0 11cbfff5
endmodule

module ALU (
  input  [31:0] A,
  input  [31:0] B,
  input  [4:0] C,
  input  [2:0] AluOp,
  output AluZero,
  output [31:0] AluOut
);

  wire [31:0] add, \or , shifter, sll, sub;

  Shifter #(.width(32)) shifter_1 (.in(B), .\dist (C), .out(sll));
  Adder #(.width(32)) adder_1 (.a(A), .b(B), .out(add));  // open: cin, cout
  Subtractor #(.width(32)) subtractor_1 (.a(A), .b(B), .out(sub));  // open: bin, bout
  assign \or  = A | B;  // OR_Gate or_1, 32 bits wide
  Shifter #(.width(32)) shifter_2 (.in(B), .\dist (5'b10000), .out(shifter));
  Multiplexer #(.select(3), .width(32), .enable("false")) multiplexer_1 (
    .in0(sll), .in1(add), .in2(sub), .in3(\or ), .in4(shifter), .out(AluOut), .sel(AluOp));  // open: in5, in6, in7
  Comparator #(.width(32)) comparator_1 (.a({32{1'b0}}), .b(AluOut), .eq(AluZero));  // open: gt, lt
endmodule

module AluController (
  input  [2:0] AluCtrl,
  input  [5:0] Function,
  output [2:0] out_3
);

  wire add_out, addu, Beq, Lui, not_1_out, not_2_out, not_3_out, not_4_out, not_5_out, not_6_out, or_out,
       Ori, shift16_out, sll_nop, sll_out, Special_nop, sub_out, subu, Sw_Lw;

  Decoder #(.select(3), .enable("false")) decoder_1 (
    .out0(Special_nop), .out1(Sw_Lw), .out2(Ori), .out3(Lui), .out4(Beq), .sel(AluCtrl));  // open: out5, out6, out7
  not not_1 (not_1_out, Function[5]);
  not not_2 (not_2_out, Function[3]);
  not not_3 (not_3_out, Function[2]);
  not not_4 (not_4_out, Function[4]);
  not not_5 (not_5_out, Function[0]);
  not not_6 (not_6_out, Function[1]);
  and _100001 (addu, Function[5], not_4_out, not_2_out, Special_nop, not_3_out, not_6_out, Function[0]);
  and _100011 (subu, Function[5], not_4_out, not_2_out, Special_nop, not_3_out, Function[1], Function[0]);
  and _000000 (sll_nop, not_1_out, not_4_out, not_2_out, Special_nop, not_3_out, not_6_out, not_5_out);
  or sll (sll_out, sll_nop, 1'b0);
  or add (add_out, addu, Sw_Lw);
  or sub (sub_out, subu, Beq);
  or \or  (or_out, Ori, 1'b0);
  or shift16 (shift16_out, Lui, 1'b0);
  Pull_Resistor pull_resistor_1 (.node(out_3));
  Priority_Encoder priority_encoder_1 (
    .in0(sll_out), .in1(add_out), .in2(sub_out), .in3(or_out), .in4(shift16_out), .out(out_3));  // open: in5, in6, in7, en_in, gs, en_out

  // Notes on the sheet:
  //   当指令为nop时，优先译码器会出现xx情况，因为此时出现未识别指令。
endmodule

module Controller (
  input  [5:0] Op,
  output RegWrite,
  output MemRead,
  output MemWrite,
  output AluSrc_R2_Im,
  output PcBranch,
  output RegDst,
  output MemToReg,
  output ExtOp,
  output Jump_sel,
  output [2:0] AluCtrl
);

  wire beq, J, lui, lw, not_1_out, not_2_out, not_3_out, not_4_out, not_5_out, not_6_out, or_1_out, ori,
       special_nop, sw;

  not not_1 (not_1_out, Op[4]);
  not not_2 (not_2_out, Op[5]);
  not not_3 (not_3_out, Op[3]);
  not not_4 (not_4_out, Op[2]);
  not not_5 (not_5_out, Op[0]);
  not not_6 (not_6_out, Op[1]);
  and _000000 (special_nop, not_2_out, not_1_out, not_3_out, not_4_out, not_6_out, not_5_out);
  and _100011 (lw, Op[5], not_1_out, not_3_out, not_4_out, Op[1], Op[0]);
  and _101011 (sw, Op[5], not_1_out, Op[3], not_4_out, Op[1], Op[0]);
  and _001101 (ori, not_2_out, not_1_out, Op[3], Op[2], not_6_out, Op[0]);
  and _001111 (lui, not_2_out, not_1_out, Op[3], Op[2], Op[1], Op[0]);
  and _000100 (beq, not_2_out, not_1_out, not_3_out, Op[2], not_6_out, not_5_out);
  and _000010 (J, not_2_out, not_1_out, not_3_out, not_4_out, Op[1], not_5_out);
  or or_1 (or_1_out, lw, sw);
  or u_RegWrite (RegWrite, special_nop, lw, ori, lui);
  or u_MemRead (MemRead, lw, 1'b0);
  or u_MemWrite (MemWrite, sw, 1'b0);
  or AluSrc (AluSrc_R2_Im, sw, lw, ori, lui);
  or PcBrach (PcBranch, beq, J);
  or u_RegDst (RegDst, special_nop, 1'b0);
  or u_MemToReg (MemToReg, lw, 1'b0);
  or u_ExtOp (ExtOp, lw, beq, sw);
  or u_Jump_sel (Jump_sel, J, 1'b0);
  Priority_Encoder priority_encoder_1 (
    .in0(special_nop), .in1(or_1_out), .in2(ori), .in3(lui), .in4(beq), .out(AluCtrl));  // open: in5, in6, in7, en_in, gs, en_out

  // Notes on the sheet:
  //   Write / Read Enable Signal
  //   Multiplexer Control Signal
  //   Alu Controller Signal
endmodule

module Extender (
  input  ExtOp,
  input  [15:0] Input,
  output [31:0] Out
);

  wire [31:0] bit_extender_1_out, bit_extender_2_out;

  assign bit_extender_1_out = {{16{1'b0}}, Input};  // Bit_Extender bit_extender_1
  assign bit_extender_2_out = {{16{Input[15]}}, Input};  // Bit_Extender bit_extender_2
  Multiplexer #(.width(32), .enable("false")) multiplexer_1 (
    .in0(bit_extender_1_out), .in1(bit_extender_2_out), .out(Out), .sel(ExtOp));
endmodule

module Nadd (
  input  [31:0] Offset_ext,
  input  [31:0] PC_4,
  output [31:0] out_3
);

  wire [31:0] shifter_1_out;

  Shifter #(.width(32)) shifter_1 (.in(Offset_ext), .\dist (5'b00010), .out(shifter_1_out));
  Adder #(.width(32)) adder_1 (.a(shifter_1_out), .b(PC_4), .out(out_3));  // open: cin, cout
endmodule

module Memory (
  input  [31:0] Addr,
  input  [31:0] WriteData,
  input  MemWrite,
  input  Clock,
  input  MemRead,
  input  Reset,
  output [31:0] out_7
);

  wire [31:0] divider_1_out;

  Divider #(.width(32)) divider_1 (.a(Addr), .b(32'h4), .out(divider_1_out));  // open: upper, rem
  RAM #(.addrWidth(5), .dataWidth(32), .bus("separate")) ram_1 (
    .addr(divider_1_out[4:0]), .din(WriteData), .data(out_7), .str(MemWrite), .clk(Clock), .ld(MemRead),
    .clr(Reset));  // open: sel
endmodule

module Jump_v3 (
  input  [31:0] PC_4,
  input  [25:0] IF_25_0,
  output [31:0] PC
);

  wire [27:0] subtractor_1_out;

  Subtractor #(.width(32)) subtractor_1 (.a(PC_4), .b(32'h4), .out({PC[31:28], subtractor_1_out}));  // open: bin, bout

  assign PC[27:0] = {IF_25_0, 2'b00};
endmodule
